# Fritzing sketch DM (saved by Fritzing 0.9.3b)
breadboards: 1

parts:
  U1 = 74HC595 SMD [package="SO16 [SMD]"]
  R1 = Resistor [tolerance=±5% resistance=330 package="2512 [SMD]"]
  R2 = Resistor [tolerance=±5% resistance=330 package="2512 [SMD]"]
  R3 = Resistor [tolerance=±5% resistance=330 package="2512 [SMD]"]
  R4 = Resistor [tolerance=±5% resistance=330 package="2512 [SMD]"]
  R5 = Resistor [tolerance=±5% resistance=330 package="2512 [SMD]"]
  R6 = Resistor [tolerance=±5% resistance=330 package="2512 [SMD]"]
  R7 = Resistor [tolerance=±5% resistance=330 package="2512 [SMD]"]
  R8 = Resistor [tolerance=±5% resistance=330 package="2512 [SMD]"]
  U2 = 74HC595 SMD [package="SO16 [SMD]"]
  R10 = Resistor [tolerance=±5% resistance=330 package="2512 [SMD]"]
  R16 = Resistor [tolerance=±5% resistance=330 package="2512 [SMD]"]
  R15 = Resistor [tolerance=±5% resistance=330 package="2512 [SMD]"]
  R13 = Resistor [tolerance=±5% resistance=330 package="2512 [SMD]"]
  R11 = Resistor [tolerance=±5% resistance=330 package="2512 [SMD]"]
  R12 = Resistor [tolerance=±5% resistance=330 package="2512 [SMD]"]
  R9 = Resistor [tolerance=±5% resistance=330 package="2512 [SMD]"]
  R14 = Resistor [tolerance=±5% resistance=330 package="2512 [SMD]"]
  J_Leds = female pin header, 3 pins [form="♀ (female)"]
  U3 = 74HC595 SMD [package="SO16 [SMD]"]
  R15_2 = Resistor [tolerance=±5% resistance=330 package="2512 [SMD]"]
  R20 = Resistor [tolerance=±5% resistance=330 package="2512 [SMD]"]
  R24 = Resistor [tolerance=±5% resistance=330 package="2512 [SMD]"]
  R17 = Resistor [tolerance=±5% resistance=330 package="2512 [SMD]"]
  R19 = Resistor [tolerance=±5% resistance=330 package="2512 [SMD]"]
  R23 = Resistor [tolerance=±5% resistance=330 package="2512 [SMD]"]
  R21 = Resistor [tolerance=±5% resistance=330 package="2512 [SMD]"]
  R18 = Resistor [tolerance=±5% resistance=330 package="2512 [SMD]"]
  U4 = 74HC595 SMD [package="SO16 [SMD]"]
  R31 = Resistor [tolerance=±5% resistance=330 package="2512 [SMD]"]
  R28 = Resistor [tolerance=±5% resistance=330 package="2512 [SMD]"]
  R32 = Resistor [tolerance=±5% resistance=330 package="2512 [SMD]"]
  R25 = Resistor [tolerance=±5% resistance=330 package="2512 [SMD]"]
  R27 = Resistor [tolerance=±5% resistance=330 package="2512 [SMD]"]
  R30 = Resistor [tolerance=±5% resistance=330 package="2512 [SMD]"]
  R29 = Resistor [tolerance=±5% resistance=330 package="2512 [SMD]"]
  R26 = Resistor [tolerance=±5% resistance=330 package="2512 [SMD]"]
  U5 = 74HC595 SMD [package="SO16 [SMD]"]
  R39 = Resistor [tolerance=±5% resistance=330 package="2512 [SMD]"]
  R36 = Resistor [tolerance=±5% resistance=330 package="2512 [SMD]"]
  R40 = Resistor [tolerance=±5% resistance=330 package="2512 [SMD]"]
  R33 = Resistor [tolerance=±5% resistance=330 package="2512 [SMD]"]
  R35 = Resistor [tolerance=±5% resistance=330 package="2512 [SMD]"]
  R38 = Resistor [tolerance=±5% resistance=330 package="2512 [SMD]"]
  R37 = Resistor [tolerance=±5% resistance=330 package="2512 [SMD]"]
  R34 = Resistor [tolerance=±5% resistance=330 package="2512 [SMD]"]
  U6 = 74HC595 SMD [package="SO16 [SMD]"]
  R47 = Resistor [tolerance=±5% resistance=330 package="2512 [SMD]"]
  R44 = Resistor [tolerance=±5% resistance=330 package="2512 [SMD]"]
  R48 = Resistor [tolerance=±5% resistance=330 package="2512 [SMD]"]
  R41 = Resistor [tolerance=±5% resistance=330 package="2512 [SMD]"]
  R43 = Resistor [tolerance=±5% resistance=330 package="2512 [SMD]"]
  R46 = Resistor [tolerance=±5% resistance=330 package="2512 [SMD]"]
  R45 = Resistor [tolerance=±5% resistance=330 package="2512 [SMD]"]
  R42 = Resistor [tolerance=±5% resistance=330 package="2512 [SMD]"]
  J1 = female pin header, 8 pins [form="♀ (female)"]
  J2 = female pin header, 8 pins [form="♀ (female)"]
  J3 = female pin header, 8 pins [form="♀ (female)"]
  J4 = female pin header, 8 pins [form="♀ (female)"]
  J6 = female pin header, 8 pins [form="♀ (female)"]
  J5 = female pin header, 8 pins [form="♀ (female)"]
  IC1 = 24LC256 [package=THT]
  R49 = Resistor [tolerance=±5% resistance=2k package="2512 [SMD]"]
  J_Mem = female pin header, 2 pins [form="♀ (female)"]

nets:
  N1: U1.Q1, R2.Pin_1
  N2: U1.Q2, R3.Pin_1
  N3: U1.Q3, R4.Pin_1
  N4: U1.Q4, R5.Pin_1
  N5: U1.Q5, R6.Pin_1
  N6: U1.Q6, R7.Pin_1
  N7: U1.Q7, R8.Pin_1
  GND: U1.GND, U1.OE, U2.GND, U2.OE, U3.GND, U3.OE, U4.GND, U4.OE, U5.GND, U5.OE, U6.GND, U6.OE, IC1.A0, IC1.A1, IC1.A2, IC1.0V, IC1.WP_-_Write_Protect
  N8: U1.Q7', U2.DS
  N9: U1.MR, U1.VCC
  N10: U1.SH_CP, U2.SH_CP, J_Leds.pin3, U3.SH_CP, U4.SH_CP, U5.SH_CP, U6.SH_CP
  N11: U1.ST_CP, U2.ST_CP, J_Leds.pin2, U3.ST_CP, U4.ST_CP, U5.ST_CP, U6.ST_CP
  N12: U1.DS, J_Leds.pin1
  N13: U1.Q0, R1.Pin_1
  N14: R1.Pin_0, J1.pin8
  N15: R2.Pin_0, J1.pin7
  N16: R3.Pin_0, J1.pin6
  N17: R4.Pin_0, J1.pin5
  N18: R5.Pin_0, J1.pin4
  N19: R6.Pin_0, J1.pin3
  N20: R7.Pin_0, J1.pin2
  N21: R8.Pin_0, J1.pin1
  N22: U2.Q1, R10.Pin_1
  N23: U2.Q2, R11.Pin_1
  N24: U2.Q3, R12.Pin_1
  N25: U2.Q4, R13.Pin_1
  N26: U2.Q5, R14.Pin_1
  N27: U2.Q6, R15.Pin_1
  N28: U2.Q7, R16.Pin_1
  N29: U2.Q7', U3.DS
  5V: U2.MR, U2.VCC, U3.MR, U3.VCC, U4.MR, U4.VCC, U5.MR, U5.VCC, U6.MR, U6.VCC
  N30: U2.Q0, R9.Pin_1
  N31: R10.Pin_0, J2.pin7
  N32: R16.Pin_0, J2.pin1
  N33: R15.Pin_0, J2.pin2
  N34: R13.Pin_0, J2.pin4
  N35: R11.Pin_0, J2.pin6
  N36: R12.Pin_0, J2.pin5
  N37: R9.Pin_0, J2.pin8
  N38: R14.Pin_0, J2.pin3
  N39: U3.Q1, R18.Pin_1
  N40: U3.Q2, R19.Pin_1
  N41: U3.Q3, R20.Pin_1
  N42: U3.Q4, R21.Pin_1
  N43: U3.Q5, R23.Pin_1
  N44: U3.Q6, R15_2.Pin_1
  N45: U3.Q7, R24.Pin_1
  N46: U3.Q7', U4.DS
  N47: U3.Q0, R17.Pin_1
  N48: R15_2.Pin_0, J3.pin2
  N49: R20.Pin_0, J3.pin5
  N50: R24.Pin_0, J3.pin1
  N51: R17.Pin_0, J3.pin8
  N52: R19.Pin_0, J3.pin6
  N53: R23.Pin_0, J3.pin3
  N54: R21.Pin_0, J3.pin4
  N55: R18.Pin_0, J3.pin7
  N56: U4.Q1, R26.Pin_1
  N57: U4.Q2, R27.Pin_1
  N58: U4.Q3, R28.Pin_1
  N59: U4.Q4, R29.Pin_1
  N60: U4.Q5, R30.Pin_1
  N61: U4.Q6, R31.Pin_1
  N62: U4.Q7, R32.Pin_1
  N63: U4.Q7', U5.DS
  N64: U4.Q0, R25.Pin_1
  N65: R31.Pin_0, J4.pin2
  N66: R28.Pin_0, J4.pin5
  N67: R32.Pin_0, J4.pin1
  N68: R25.Pin_0, J4.pin8
  N69: R27.Pin_0, J4.pin6
  N70: R30.Pin_0, J4.pin3
  N71: R29.Pin_0, J4.pin4
  N72: R26.Pin_0, J4.pin7
  N73: U5.Q1, R34.Pin_1
  N74: U5.Q2, R35.Pin_1
  N75: U5.Q3, R36.Pin_1
  N76: U5.Q4, R37.Pin_1
  N77: U5.Q5, R38.Pin_1
  N78: U5.Q6, R39.Pin_1
  N79: U5.Q7, R40.Pin_1
  N80: U5.Q7', U6.DS
  N81: U5.Q0, R33.Pin_1
  N82: R39.Pin_0, J6.pin2
  N83: R36.Pin_0, J6.pin5
  N84: R40.Pin_0, J6.pin1
  N85: R33.Pin_0, J6.pin8
  N86: R35.Pin_0, J6.pin6
  N87: R38.Pin_0, J6.pin3
  N88: R37.Pin_0, J6.pin4
  N89: R34.Pin_0, J6.pin7
  N90: U6.Q1, R42.Pin_1
  N91: U6.Q2, R43.Pin_1
  N92: U6.Q3, R44.Pin_1
  N93: U6.Q4, R45.Pin_1
  N94: U6.Q5, R46.Pin_1
  N95: U6.Q6, R47.Pin_1
  N96: U6.Q7, R48.Pin_1
  N97: U6.Q0, R41.Pin_1
  N98: R47.Pin_0, J5.pin2
  N99: R44.Pin_0, J5.pin5
  N100: R48.Pin_0, J5.pin1
  N101: R41.Pin_0, J5.pin8
  N102: R43.Pin_0, J5.pin6
  N103: R46.Pin_0, J5.pin3
  N104: R45.Pin_0, J5.pin4
  N105: R42.Pin_0, J5.pin7
  N106: IC1.SDA_-_I2C_Data, R49.Pin_1, J_Mem.pin2
  N107: IC1.SCL_-_I2C_Clock, J_Mem.pin1
  3.3V: IC1.+V, R49.Pin_0
